# Fritzing sketch Project11 Fritzing (saved by Fritzing 0.8.7b)
breadboards: 1

parts:
  Part1 = Arduino Uno (Rev3) - ICSP
  LED1 = RGB LED (com. anode, rbg) [package="5 mm [THT]"]
  J1 = Piezo Speaker
  R2 = Resistor [tolerance=±5% resistance=10k package="0603 [SMD]"]
  DHT1 = DHT11 Humitidy and Temperature Sensor
  PIR1 = PIR sensor
  R3 = PHOTOCELL [package=photocell]
  S1 = Pushbutton [package="[SMD]"]
  R4 = Resistor [tolerance=±5% resistance=10k package="0603 [SMD]"]
  R7 = Resistor [tolerance=±5% resistance=220 package="0603 [SMD]"]
  R8 = Resistor [tolerance=±5% resistance=220 package="0603 [SMD]"]
  R9 = Resistor [tolerance=±5% resistance=220 package="0603 [SMD]"]
  LED2 = smd LED [color="White (4500K)" package="0603 [SMD]"]
  LED3 = smd LED [color="White (4500K)" package="0603 [SMD]"]
  LED4 = smd LED [color="Yellow (585nm)" package="0603 [SMD]"]
  LED5 = smd LED [color="Yellow (592nm)" package="0603 [SMD]"]
  LED6 = smd LED [color="Red (633nm)" package="0603 [SMD]"]
  LED7 = smd LED [color="Red (633nm)" package="0603 [SMD]"]
  R10 = Resistor [tolerance=±5% resistance=220 package="0603 [SMD]"]
  R11 = Resistor [tolerance=±5% resistance=220 package="0603 [SMD]"]
  R12 = Resistor [tolerance=±5% resistance=220 package="0603 [SMD]"]
  R13 = Resistor [tolerance=±5% resistance=220 package="0603 [SMD]"]
  R14 = Resistor [tolerance=±5% resistance=220 package="0603 [SMD]"]
  R15 = Resistor [tolerance=±5% resistance=220 package="0603 [SMD]"]

nets:
  N1: Part1.A0, R3.P$2, R4.Pin_1
  N2: Part1.D8, R15.Pin_0
  N3: Part1.D9_PWM, R14.Pin_0
  N4: Part1.D10_PWM/SS, R13.Pin_0
  N5: Part1.D11_PWM/MOSI, R12.Pin_0
  N6: Part1.D12/MISO, R11.Pin_0
  N7: Part1.D13/SCK, R10.Pin_0
  N8: Part1.D0/RX, J1.pin2
  N9: Part1.D1/TX, R2.Pin_1, S1.Pin_1, S1.Pin_2
  N10: Part1.D2, R7.Pin_0
  N11: Part1.D3_PWM, R8.Pin_0
  N12: Part1.D4, R9.Pin_0
  N13: Part1.D5_PWM, DHT1.DATA
  N14: Part1.D6_PWM, PIR1.SIG
  VDD: Part1.5V, LED1.common_anode, DHT1.VDD, PIR1.VDD, R3.P$1, S1.Pin_3, S1.Pin_4
  GND: Part1.GND, J1.pin1, R2.Pin_0, DHT1.GND, PIR1.GND, R4.Pin_0, LED2.cathode, LED3.cathode, LED4.cathode, LED5.cathode, LED6.cathode, LED7.cathode
  N15: LED1.red_cathode, R9.Pin_1
  N16: LED1.blue_cathode, R8.Pin_1
  N17: LED1.green_cathode, R7.Pin_1
  N18: LED2.anode, R10.Pin_1
  N19: LED3.anode, R11.Pin_1
  N20: LED4.anode, R12.Pin_1
  N21: LED5.anode, R13.Pin_1
  N22: LED6.anode, R14.Pin_1
  N23: LED7.anode, R15.Pin_1

custom parts:
  DHT11 Humitidy and Temperature Sensor: DHT11 Humidity and Temperature Sensor
