# Fritzing sketch Project11b Fritzing (saved by Fritzing 0.8.7b)
breadboards: 1

parts:
  Part1 = Arduino Uno (Rev3)
  R1 = Resistor [package="0402 [SMD]"]
  S1 = Momentary Switch [package=ksa_sealed_tac_switch]
  R2 = Resistor [tolerance=±5% resistance=10k package="0603 [SMD]"]
  LED2 = RGB LED - (4 legs) [package="5 mm [THT]"]
  PIR1 = PIR sensor
  DHT1 = DHT11 Humitidy and Temperature Sensor
  J1 = Piezo Speaker
  R3 = Photocell (LDR) [package=THT]
  R4 = Resistor [tolerance=±5% resistance=10k package="0603 [SMD]"]
  LED3 = LED - 5mm [color="Green (555nm)" package="5 mm [THT]"]  # not connected
  LED4 = LED - 5mm [color="Green (555nm)" package="5 mm [THT]"]
  LED5 = LED - 5mm [color="Yellow (585nm)" package="5 mm [THT]"]
  LED6 = LED - 5mm [color="Yellow (585nm)" package="5 mm [THT]"]  # not connected
  LED7 = LED - 5mm [color="Red (633nm)" package="5 mm [THT]"]
  LED8 = LED - 5mm [color="Red (633nm)" package="5 mm [THT]"]  # not connected
  R6 = Resistor [tolerance=±5% resistance=10k package="0603 [SMD]"]

nets:
  N1: Part1.A5/SCL, R3.pin_1, R4.Pin_0
  N2: Part1.D8, PIR1.SIG
  GND: Part1.GND, R2.Pin_1, PIR1.GND, DHT1.GND, R4.Pin_1, R6.Pin_1
  N3: Part1.D0/RX, S1.2, R2.Pin_0
  N4: Part1.D1/TX, LED2.green_cathode
  N5: Part1.D2, LED2.red_cathode
  N6: Part1.D3_PWM, J1.pin2
  N7: Part1.D7, DHT1.DATA
  VDD: Part1.5V, R1.Pin_1, S1.4, PIR1.VDD, DHT1.VDD, J1.pin1, R3.pin_0
  N8: R1.Pin_0, LED2.common_anode
  N9: LED4.cathode, LED5.cathode, LED7.cathode, R6.Pin_0

custom parts:
  DHT11 Humitidy and Temperature Sensor: DHT11 Humidity and Temperature Sensor
