# Fritzing sketch Project1a Fritzing (saved by Fritzing 0.9.0b)
breadboards: 1

parts:
  Part1 = Arduino Uno (Rev3)
  R1 = Resistor [package="0402 [SMD]"]
  LED1 = smd LED [color="Red (633nm)" package="0805 [SMD]"]
  S1 = Momentary Switch [package=ksa_sealed_tac_switch]
  R2 = Resistor [tolerance=±5% resistance=10k package="0603 [SMD]"]

nets:
  N1: Part1.D13/SCK, R1.Pin_0
  N2: Part1.D2, S1.1
  N3: Part1.5V, S1.4
  N4: Part1.GND, LED1.cathode, R2.Pin_1
  N5: R1.Pin_1, LED1.anode
  N6: S1.2, R2.Pin_0
