# Fritzing sketch Project4 Fritzing (saved by Fritzing 0.9.0b)
breadboards: 1

parts:
  Part1 = Arduino Uno (Rev3)
  LED1 = smd LED [color="Red (633nm)" package="0805 [SMD]"]
  DHT1 = DHT11 Humitidy and Temperature Sensor
  R3 = Resistor [tolerance=±5% resistance=10k package=THT]
  LED2 = smd LED [color="Yellow (585nm)" package="0603 [SMD]"]
  LED3 = smd LED [color="Green (555nm)" package="0603 [SMD]"]
  R4 = Resistor [tolerance=±5% resistance=220 package="1206 [SMD]"]
  R5 = Resistor [tolerance=±5% resistance=220 package="1206 [SMD]"]
  R6 = Resistor [tolerance=±5% resistance=220 package="1206 [SMD]"]

nets:
  N1: Part1.D11_PWM/MOSI, LED1.anode
  N2: Part1.D12/MISO, LED2.anode
  N3: Part1.D13/SCK, LED3.anode
  N4: Part1.D2, DHT1.DATA, R3.Pin_0
  5V: Part1.5V, DHT1.VDD, R3.Pin_1
  GND: Part1.GND, DHT1.GND, R4.Pin_1, R5.Pin_1, R6.Pin_1
  N5: LED1.cathode, R6.Pin_0
  N6: LED2.cathode, R5.Pin_0
  N7: LED3.cathode, R4.Pin_0

custom parts:
  DHT11 Humitidy and Temperature Sensor: DHT11 Humidity and Temperature Sensor
