# Fritzing sketch Project7 Fritzing (saved by Fritzing 0.9.0b)
breadboards: 1

parts:
  Part1 = Arduino Uno (Rev3)
  R1 = Resistor [package="0402 [SMD]"]
  S1 = Momentary Switch [package=ksa_sealed_tac_switch]
  R2 = Resistor [tolerance=±5% resistance=10k package="0603 [SMD]"]
  LED2 = RGB LED - (4 legs) [package="5 mm [THT]"]

nets:
  N1: Part1.D9_PWM, LED2.blue_cathode
  N2: Part1.D10_PWM/SS, LED2.green_cathode
  N3: Part1.D11_PWM/MOSI, LED2.red_cathode
  N4: Part1.D2, S1.2, R2.Pin_0
  N5: Part1.5V, R1.Pin_0, S1.4
  N6: Part1.GND, R2.Pin_1
  N7: R1.Pin_1, LED2.common_anode
